// Digital circuit MemoryManagement.dig as structural Verilog
module MemoryManagement (
  input  [31:0] PC_In,
  input  [31:0] PD_In,
  input  [5:0] Dev,
  input  [15:0] Addr,
  input  Push,
  input  [31:0] Mem_In,
  input  Mem_Write,
  input  Pop,
  input  CLK,
  output PC_Write,
  output [31:0] PC_Out,
  output PD_Write,
  output [31:0] PD_Out,
  output [31:0] Mem_Out,
  output [31:0] Stack_Top
);

  wire delay_1_out, device0_1_p14, device0_1_p15, device0_1_p16;

  Delay delay_1 (.in(CLK), .out(delay_1_out));
  // Device0 device0_1: pin names not known; wires that end beside it: CLK, Addr, Dev, Mem_In, Mem_Write, PC_In, PD_In, CLK, Addr, Dev, Mem_In, Mem_Write, Stack_Top, device0_1_p14, device0_1_p15, device0_1_p16, Mem_Out, PC_Write, PD_Write
  // Device1 device1_1: pin names not known; wires that end beside it: CLK, Addr, Dev, Mem_In, Mem_Write, CLK, Addr, Dev, Mem_In, Mem_Write, device0_1_p16, device0_1_p15, device0_1_p14, Stack_Top, Mem_Out, CLK, Addr, Dev, Mem_In, Mem_Write

  assign PC_Out = Mem_Out;
  assign PD_Out = Mem_Out;
endmodule
